// Logisim project MIPS_Processor.circ as structural Verilog: 5 circuits, main circuit main
module main (
  output [7:0] out_1
);

  wire undriven, undriven_2, undriven_3, undriven_4;
  wire [3:0] instruction_memory_1_instruction, multiplexer_1_out;
  wire [7:0] pc_module_1_currentpc;
  wire [15:12] instruction_memory_1_instruction_2;

  PC_Module pc_module_1 (
    .jump_address(out_1), .branch_offset(instruction_memory_1_instruction), .jumpControl(undriven_2),
    .branchTaken(undriven), .currentPC(pc_module_1_currentpc));  // open: PC_register_enable, PC_register_reset
  Instruction_Memory instruction_memory_1 (
    .currentPC(pc_module_1_currentpc),
    .instruction({instruction_memory_1_instruction_2, out_1, instruction_memory_1_instruction}));
  Multiplexer #(.width(4)) multiplexer_1 (
    .in0(instruction_memory_1_instruction), .in1(out_1[3:0]), .out(multiplexer_1_out), .sel(undriven_3));
  Register_File register_file_1 (
    .ReadReg1(out_1[7:4]), .RegWriteControl(undriven_4), .WriteReg(multiplexer_1_out), .ReadReg2(out_1[3:0]));  // open: Register_Reset, WriteData, ReadData1, ReadData2

  // Notes on the sheet:
  //   From Control Unit
  //   OpCode goes to Control Unit
  //   jump address
  //   Branch, Jump, and Shift not implemented yet.
endmodule

module PC_Module (
  input  PC_register_enable,
  input  PC_register_reset,
  input  [7:0] jump_address,
  input  [3:0] branch_offset,
  input  jumpControl,
  input  branchTaken,
  output [7:0] currentPC
);

  wire PC_clock_out;
  wire [7:0] adder_1_out, adder_2_out, bit_extender_1_out, multiplexer_1_out, multiplexer_2_out;

  Clock PC_clock (.out(PC_clock_out));
  Register PC_Register (
    .D(multiplexer_2_out), .en(PC_register_enable), .clk(PC_clock_out), .Q(currentPC), .clr(PC_register_reset));
  assign bit_extender_1_out = {{4{branch_offset[3]}}, branch_offset};  // Bit_Extender bit_extender_1
  Adder adder_1 (.a(currentPC), .b({8{1'b0}}), .out(adder_1_out), .cin(1'b1));  // open: cout
  Adder adder_2 (.a(adder_1_out), .b(bit_extender_1_out), .out(adder_2_out), .cin(1'b0));  // open: cout
  Multiplexer #(.width(8)) multiplexer_1 (
    .in0(adder_1_out), .in1(adder_2_out), .out(multiplexer_1_out), .sel(branchTaken));
  Multiplexer #(.width(8)) multiplexer_2 (
    .in0(multiplexer_1_out), .in1(jump_address), .out(multiplexer_2_out), .sel(jumpControl));

  // Notes on the sheet:
  //   PC_register_enable: initial=0x1
  //   branch_offset_sign_extension
  //   PC Module
  //   PC + 1
  //   PC + 1 + branch_offset
endmodule

module Instruction_Memory (
  input  [7:0] currentPC,
  output [15:0] instruction
);

  ROM #(.dataWidth(16)) Instruction_Memory (.addr(currentPC), .data(instruction));

  // Notes on the sheet:
  //   PC
endmodule

module Register_File (
  input  Register_Reset,
  input  [3:0] WriteData,
  input  [3:0] ReadReg1,
  input  RegWriteControl,
  input  [3:0] WriteReg,
  input  [3:0] ReadReg2,
  output [3:0] ReadData1,
  output [3:0] ReadData2
);

  wire clock_1_out;
  wire [3:0] demultiplexer_1_out0, demultiplexer_1_out1, demultiplexer_1_out2, demultiplexer_1_out3,
       demultiplexer_1_out4, demultiplexer_1_out5, t0_q, t1_q, t2_q, t3_q, t4_q, zero_q;

  Demultiplexer #(.enable("true"), .select(4), .width(4)) demultiplexer_1 (
    .out0(demultiplexer_1_out0), .out1(demultiplexer_1_out1), .out2(demultiplexer_1_out2),
    .out3(demultiplexer_1_out3), .out4(demultiplexer_1_out4), .out5(demultiplexer_1_out5), .in(WriteData),
    .sel(WriteReg), .en(RegWriteControl));  // open: out6, out7, out8, out9, out10, out11, out12, out13, out14, out15
  Clock clock_1 (.out(clock_1_out));
  Register #(.width(4)) zero (.D(4'b0000), .en(1'b1), .clk(clock_1_out), .Q(zero_q), .clr(Register_Reset));
  Register #(.width(4)) t0 (.D(demultiplexer_1_out1), .en(1'b1), .clk(clock_1_out), .Q(t0_q), .clr(Register_Reset));
  Register #(.width(4)) t1 (.D(demultiplexer_1_out2), .en(1'b1), .clk(clock_1_out), .Q(t1_q), .clr(Register_Reset));
  Register #(.width(4)) t2 (.D(demultiplexer_1_out3), .en(1'b1), .clk(clock_1_out), .Q(t2_q), .clr(Register_Reset));
  Register #(.width(4)) t3 (.D(demultiplexer_1_out4), .en(1'b1), .clk(clock_1_out), .Q(t3_q), .clr(Register_Reset));
  Register #(.width(4)) t4 (.D(demultiplexer_1_out5), .en(1'b1), .clk(clock_1_out), .Q(t4_q), .clr(Register_Reset));
  Multiplexer #(.select(4), .width(4)) multiplexer_1 (
    .in0(zero_q), .in1(t0_q), .in2(t1_q), .in3(t2_q), .in4(t3_q), .in5(t4_q), .in6(4'b0000), .in7(4'b0000),
    .in8(4'b0000), .in9(4'b0000), .in10(4'b0000), .in11(4'b0000), .in12(4'b0000), .in13(4'b0000),
    .in14(4'b0000), .in15(4'b0000), .out(ReadData1), .sel(ReadReg1));
  Multiplexer #(.select(4), .width(4)) multiplexer_2 (
    .in0(zero_q), .in1(t0_q), .in2(t1_q), .in3(t2_q), .in4(t3_q), .in5(t4_q), .in6(4'b0000), .in7(4'b0000),
    .in8(4'b0000), .in9(4'b0000), .in10(4'b0000), .in11(4'b0000), .in12(4'b0000), .in13(4'b0000),
    .in14(4'b0000), .in15(4'b0000), .out(ReadData2), .sel(ReadReg2));

  // Notes on the sheet:
  //   Register_Enable
  //   zero write ignored
  //   Register File
endmodule

module MEM (
  input  MEM_READ,
  input  MEM_WRITE,
  input  CLK,
  input  [3:0] ALU_RESULT,
  input  [3:0] WRITE_DATA,
  output [3:0] MEMTOREG
);

  wire [7:0] bit_extender_1_out;

  assign bit_extender_1_out = {{4{ALU_RESULT[3]}}, ALU_RESULT};  // Bit_Extender bit_extender_1
  RAM #(.dataWidth(4)) ram_1 (
    .addr(bit_extender_1_out), .we(MEM_WRITE), .oe(MEM_READ), .clk(CLK), .din(WRITE_DATA), .dout(MEMTOREG));
endmodule
